# Fritzing sketch two-buttons-poten-uniLed (saved by Fritzing 0.9.3b)
breadboards: 1

parts:
  Componente2 = Arduino Uno (Rev3)
  LED13 = LED - 5mm [color="Red (633nm)" package="5 mm [THT]"]
  R12 = Resistor [tolerance=±5% resistance=330 package=THT]
  S1 = Momentary Switch [package=ksa_sealed_tac_switch]
  S2 = Momentary Switch [package=ksa_sealed_tac_switch]
  R13 = Rotary Potentiometer (Small) [maximum_resistance=100kΩ package=THT]

nets:
  N1: Componente2.A0, R13.wiper
  N2: Componente2.D9_PWM, LED13.anode
  N3: Componente2.GND, R12.Pin_1, S1.2, S2.2, R13.leg2
  N4: Componente2.D2, S1.4
  N5: Componente2.D3_PWM, S2.4
  N6: Componente2.5V, R13.leg1
  N7: LED13.cathode, R12.Pin_0
